# Fritzing sketch ldr (saved by Fritzing 0.9.0b)
breadboards: 1

parts:
  Part2 = Spark Core (v1.0)
  R1 = Photocell (LDR) [package=THT]
  R2 = Resistor [tolerance=±5% resistance=1k package="1206 [SMD]"]

nets:
  N1: Part2.A0, R1.pin_1, R2.Pin_1
  N2: Part2.GND, R1.pin_0
  N3: Part2.VIN, R2.Pin_0
