# Fritzing sketch servo (saved by Fritzing 0.9.0b)
breadboards: 1

parts:
  Part1 = Spark Core (v1.0)
  J1 = Basic Servo
  C1 = Electrolytic Capacitor [capacitance=1µF package="100 mil [THT, electrolytic]"]

nets:
  N1: Part1.A0, J1.pulse
  GND: Part1.GND, J1.gnd, C1.-
  VIN: Part1.VIN, J1.vcc, C1.+
